// Logisim project Sagui.circ as structural Verilog: 8 circuits, main circuit main
module main (
);

  wire CLK, S_B, S_End, S_Mem, WE_M, WE_R, Z;
  wire [1:0] multiplexer_2_out, Programa_data, Programa_data_2, S_PC;
  wire [3:0] Imm, S_ULA;
  wire [7:0] adder_1_out, adder_2_out, bit_extender_1_out, Imm_Est, Mem_Dados_dout, multiplexer_1_out,
       multiplexer_3_out, multiplexer_4_out, PC_q, Reg_Bank_a, Reg_Bank_b, ULA_M_s;
  wire [11:9] Controle_data;

  Multiplexer #(.select(2), .width(8)) multiplexer_1 (
    .in0(adder_1_out), .in1(Reg_Bank_b), .in3(adder_2_out), .out(multiplexer_1_out), .sel(S_PC));  // open: in2
  Clock clock_1 (.out(CLK));
  Register PC (.D(multiplexer_1_out), .en(1'b1), .clk(CLK), .Q(PC_q));  // open: clr
  assign bit_extender_1_out = {{4{Imm[3]}}, Imm};  // Bit_Extender bit_extender_1
  Adder adder_1 (.a(PC_q), .b(8'h1), .out(adder_1_out));  // open: cin, cout
  Adder adder_2 (.a(PC_q), .b(bit_extender_1_out), .out(adder_2_out));  // open: cin, cout
  ROM Programa (.addr(PC_q), .data({Programa_data_2, Programa_data, Imm}));
  assign Imm_Est = {{4{1'b0}}, Imm};  // Bit_Extender bit_extender_2
  Multiplexer #(.width(2)) multiplexer_2 (.in0(2'b00), .in1(Imm[3:2]), .out(multiplexer_2_out), .sel(S_End));
  ROM #(.addrWidth(4), .dataWidth(12)) Controle (
    .addr({Programa_data_2, Programa_data}), .data({Controle_data, S_End, WE_R, S_B, S_ULA, WE_M, S_Mem}));
  Banco_de_registradores Reg_Bank (
    .WE(WE_R), .CLK(CLK), .End_a(multiplexer_2_out), .End_b(Imm[1:0]), .W(multiplexer_4_out), .A(Reg_Bank_a),
    .B(Reg_Bank_b));
  Multiplexer #(.width(8)) multiplexer_3 (.in0(Reg_Bank_b), .in1(Imm_Est), .out(multiplexer_3_out), .sel(S_B));
  ULA ULA_M (.A(Reg_Bank_a), .B(multiplexer_3_out), .ULA_S(S_ULA), .S(ULA_M_s), .Zero(Z));
  BR_JP_LG Log_PC (
    .S_PC_S(Controle_data[9]), .IS_BR(Controle_data[10]), .IS_JP(Controle_data[11]), .Zero(Z), .s0(S_PC[0]),
    .s1(S_PC[1]));
  RAM Mem_Dados (.addr(Reg_Bank_b), .we(WE_M), .oe(1'b1), .clk(CLK), .din(Reg_Bank_a), .dout(Mem_Dados_dout));
  Multiplexer #(.width(8)) multiplexer_4 (.in0(Mem_Dados_dout), .in1(ULA_M_s), .out(multiplexer_4_out), .sel(S_Mem));

  // Notes on the sheet:
  //   contents of Programa (hex, n*v repeats v):
  //   85 64 82 68 6e 99 71 a2 b6 cc df ed fd 53 4b 85 71 64 70 80 4 11 71 89 24 31 70 80 64 68 6c 84 5c 64
  //   72 8d 68 89 6c 70 81 6 55 a4 2f 2a
  //   contents of Controle (hex, n*v repeats v):
  //   525 625 801 a01 180 103 1a9 dd e1 181 185 189 18d 191 195 199
endmodule

module ULA (
  input  [7:0] A,
  input  [7:0] B,
  input  [3:0] ULA_S,
  output [7:0] S,
  output Zero
);

  wire comparator_1_eq;
  wire [7:0] adder_1_out, and_1_out, bit_extender_1_out, Concat_high_s, Concat_low_s, Desloc_dir_s,
       Desloc_esq_s, not_1_out, or_1_out, subtractor_1_out;

  Adder adder_1 (.a(A), .b(B), .out(adder_1_out));  // open: cin, cout
  Subtractor subtractor_1 (.a(A), .b(B), .out(subtractor_1_out));  // open: bin, bout
  assign and_1_out = A & B;  // AND_Gate and_1, 8 bits wide
  assign or_1_out = A | B;  // OR_Gate or_1, 8 bits wide
  assign not_1_out = ~A;  // NOT_Gate not_1, 8 bits wide
  Deslocador_esq_main Desloc_esq (.A(A), .B(B), .S(Desloc_esq_s));
  Deslocador_dir_main Desloc_dir (.A(A), .B(B), .S(Desloc_dir_s));
  Concatenador_High Concat_high (.A(A), .B(B), .S(Concat_high_s));
  Concatenador_Low Concat_low (.A(A), .B(B), .S(Concat_low_s));
  Comparator comparator_1 (.a(A), .b({8{1'b0}}), .eq(comparator_1_eq));  // open: gt, lt
  assign bit_extender_1_out = {{7{1'b0}}, comparator_1_eq};  // Bit_Extender bit_extender_1
  Multiplexer #(.select(4), .width(8)) multiplexer_1 (
    .in0(adder_1_out), .in1(subtractor_1_out), .in2(and_1_out), .in3(or_1_out), .in4(not_1_out),
    .in5(Desloc_esq_s), .in6(Desloc_dir_s), .in7(Concat_high_s), .in8(Concat_low_s),
    .in9(bit_extender_1_out), .in10(B), .out(S), .sel(ULA_S));  // open: in11, in12, in13, in14, in15

  assign Zero = S[0];
endmodule

module Banco_de_registradores (
  input  WE,
  input  CLK,
  input  [1:0] End_a,
  input  [1:0] End_b,
  input  [7:0] W,
  output [7:0] A,
  output [7:0] B
);

  wire demultiplexer_1_out0, demultiplexer_1_out1, demultiplexer_1_out2, demultiplexer_1_out3;
  wire [7:0] register_1_q, register_2_q, register_3_q, register_4_q;

  Demultiplexer #(.select(2)) demultiplexer_1 (
    .out0(demultiplexer_1_out0), .out1(demultiplexer_1_out1), .out2(demultiplexer_1_out2),
    .out3(demultiplexer_1_out3), .in(WE), .sel(End_a));
  Register register_1 (.D(W), .en(demultiplexer_1_out2), .clk(CLK), .Q(register_1_q));  // open: clr
  Register register_2 (.D(W), .en(demultiplexer_1_out3), .clk(CLK), .Q(register_2_q));  // open: clr
  Register register_3 (.D(W), .en(demultiplexer_1_out0), .clk(CLK), .Q(register_3_q));  // open: clr
  Register register_4 (.D(W), .en(demultiplexer_1_out1), .clk(CLK), .Q(register_4_q));  // open: clr
  Multiplexer #(.select(2), .width(8)) multiplexer_1 (
    .in0(register_3_q), .in1(register_4_q), .in2(register_1_q), .in3(register_2_q), .out(A), .sel(End_a));
  Multiplexer #(.select(2), .width(8)) multiplexer_2 (
    .in0(register_3_q), .in1(register_4_q), .in2(register_1_q), .in3(register_2_q), .out(B), .sel(End_b));
endmodule

module Deslocador_esq_main (
  input  [7:0] A,
  input  [7:0] B,
  output [7:0] S
);

  wire or_1_out;
  wire [7:0] shifter_1_out;

  Shifter shifter_1 (.in(A), .\dist (B[2:0]), .out(shifter_1_out));
  or or_1 (or_1_out, B[3], B[4], B[5], B[6], B[7]);
  Multiplexer #(.width(8)) multiplexer_1 (.in0(shifter_1_out), .in1({8{1'b0}}), .out(S), .sel(or_1_out));
endmodule

module Deslocador_dir_main (
  input  [7:0] A,
  input  [7:0] B,
  output [7:0] S
);

  wire or_1_out;
  wire [7:0] shifter_1_out;

  Shifter #(.shift("lr")) shifter_1 (.in(A), .\dist (B[2:0]), .out(shifter_1_out));
  or or_1 (or_1_out, B[3], B[4], B[5], B[6], B[7]);
  Multiplexer #(.width(8)) multiplexer_1 (.in0(shifter_1_out), .in1({8{1'b0}}), .out(S), .sel(or_1_out));
endmodule

module Concatenador_High (
  input  [7:0] A,
  input  [7:0] B,
  output [7:0] S
);


  assign S = {B[3:0], A[3:0]};
endmodule

module Concatenador_Low (
  input  [7:0] A,
  input  [7:0] B,
  output [7:0] S
);


  assign S = {A[7:4], B[3:0]};
endmodule

module BR_JP_LG (
  input  S_PC_S,
  input  IS_BR,
  input  IS_JP,
  input  Zero,
  output s0,
  output s1
);

  wire and_1_out;

  and and_1 (and_1_out, IS_BR, Zero);
  or or_1 (s0, and_1_out, IS_JP);

  assign s1 = S_PC_S;
endmodule
